# Fritzing sketch sensor PIR bajo cama (saved by Fritzing 0.9.3b)

parts:
  PIR1 = PIR sensor
  Q1 = NPN-Transistor [package="TO92 [THT]"]
  R1 = Resistor [tolerance=±5% resistance=22k package=THT]
  U1 = Voltage Regulator - 5V [package="TO220 [THT]"]
  C1 = Electrolytic Capacitor [capacitance=1µF package="100 mil [THT, electrolytic]"]
  J1 = Screw terminal - 2 pins [package=THT]
  J2 = Screw terminal - 2 pins [package=THT]

nets:
  N1: PIR1.VDD, U1.output_voltage, C1.+
  N2: PIR1.SIG, R1.Pin_0
  GND: PIR1.GND, Q1.E, U1.GND, C1.-, J2.pin2
  N3: Q1.B, J1.pin1
  N4: Q1.C, R1.Pin_1
  N5: U1.input_voltage, J1.pin2, J2.pin1

notes:
  12V
  7805
  330uF / 10V
  PIR HC-SR501
  22K
  BD137
  e c b
  Tira led 12V
